# Fritzing sketch ElectronicSchema (saved by Fritzing 0.9.3b)

parts:
  DFRobot_DFPlayer_Mini1 = DFRobot DFPlayer Mini [part_number=DFR0299]
  SP1 = SPEAKER [package=pcb_mount_speaker]
  S1 = Round Pushbutton
  U1 = BATTERY-2 [package=battery-aaa]
  U2 = BATTERY-2 [package=battery-aaa]
  U3 = BATTERY-2 [package=battery-aaa]

nets:
  N1: DFRobot_DFPlayer_Mini1.VCC, S1.leg1
  N2: DFRobot_DFPlayer_Mini1.SPK_1, SP1.-
  N3: DFRobot_DFPlayer_Mini1.GND-1, DFRobot_DFPlayer_Mini1.GND-2, DFRobot_DFPlayer_Mini1.ADKEY_1, U3.-1
  N4: DFRobot_DFPlayer_Mini1.SPK_2, SP1.+
  N5: S1.leg0, U1.+1
  N6: U1.-1, U2.+1
  N7: U2.-1, U3.+1

notes:
  Auto-play
